// Logisim project processor.circ as structural Verilog: 11 circuits, main circuit main
module main (
);

  wire alu_1_out_11, alu_1_out_12, alu_1_out_13, alu_1_out_14, and_1_out, and_2_out, and_3_out, button_1_out,
       button_2_out, clock_1_out, decoder_1_a_wr, decoder_1_alu_flag, decoder_1_alu_rd, decoder_1_asel,
       decoder_1_b_wr, decoder_1_ir_wrt, decoder_1_mem_pc, decoder_1_mem_read, decoder_1_mem_t,
       decoder_1_mem_write, decoder_1_pc_inc, decoder_1_pc_wrt, decoder_1_t_rd, decoder_1_t_wr, nor_1_out,
       nor_2_out, not_1_out, not_2_out, not_3_out, or_1_out;
  wire [1:0] decoder_1_bsel;
  wire [2:0] decoder_1_outsel;
  wire [5:0] controlled_buffer_1_out;
  wire [6:6] controlled_buffer_1_out_2;
  wire [7:0] decoder_1_dbus, pc_1_out_6, reg_1_out_5, reg_1_out_6, reg_2_out_5, reg_3_out_5, reg_4_out_5,
       reg_4_out_6, vidmem_1_out_7, vidmem_1_out_8, vidmem_1_out_9, vidmem_1_out_10, vidmem_1_out_11,
       vidmem_1_out_12, vidmem_1_out_13, vidmem_1_out_14;
  wire [7:7] controlled_buffer_1_out_3;

  // Probe on reg_1_out_5
  Button button_1 (.out(button_1_out));
  REG reg_1 (
    .in_1(decoder_1_dbus), .in_2(clock_1_out), .in_3(decoder_1_ir_wrt), .out_5(reg_1_out_5),
    .out_6(reg_1_out_6));  // open: in_4, out_7
  decoder decoder_1 (
    .in_3(button_2_out), .in_4(clock_1_out), .in_5(alu_1_out_11), .in_6(alu_1_out_12), .in_7(alu_1_out_13),
    .in_8(alu_1_out_14), .in_9(nor_1_out), .in_10(not_2_out), .in_11(nor_2_out), .in_12(not_3_out),
    .in_1(reg_1_out_5), .in_2(reg_1_out_6), .in_13(button_1_out), .PC_INC(decoder_1_pc_inc),
    .PC_WRT(decoder_1_pc_wrt), .MEM_PC(decoder_1_mem_pc), .MEM_T(decoder_1_mem_t),
    .MEM_READ(decoder_1_mem_read), .MEM_WRITE(decoder_1_mem_write), .IR_WRT(decoder_1_ir_wrt),
    .A_WR(decoder_1_a_wr), .B_WR(decoder_1_b_wr), .T_RD(decoder_1_t_rd), .T_WR(decoder_1_t_wr),
    .ALU_RD(decoder_1_alu_rd), .ALU_FLAG(decoder_1_alu_flag), .ASEL(decoder_1_asel), .BSEL(decoder_1_bsel),
    .OUTSEL(decoder_1_outsel), .DBUS(decoder_1_dbus));
  // Probe on decoder_1_dbus
  Button button_2 (.out(button_2_out));
  Clock clock_1 (.out(clock_1_out));
  PC pc_1 (
    .in_1(decoder_1_dbus), .in_4(decoder_1_pc_inc), .in_5(decoder_1_pc_wrt), .in_2(button_2_out),
    .in_3(clock_1_out), .out_6(pc_1_out_6));
  REG reg_2 (
    .in_1(decoder_1_dbus), .in_2(clock_1_out), .in_3(decoder_1_t_wr), .in_4(decoder_1_t_rd),
    .out_5(reg_2_out_5), .out_7(decoder_1_dbus));  // open: out_6
  REG reg_3 (
    .in_1(decoder_1_dbus), .in_2(clock_1_out), .in_3(decoder_1_a_wr), .out_5(reg_3_out_5));  // open: in_4, out_6, out_7
  REG reg_4 (
    .in_1(decoder_1_dbus), .in_2(clock_1_out), .in_3(decoder_1_b_wr), .out_5(reg_4_out_5), .out_6(reg_4_out_6));  // open: in_4, out_7
  // Probe on pc_1_out_6
  assign {controlled_buffer_1_out_3[7], controlled_buffer_1_out_2[6], controlled_buffer_1_out} = decoder_1_mem_pc ? pc_1_out_6 : 8'bz;  // Controlled_Buffer controlled_buffer_1
  assign {controlled_buffer_1_out_3[7], controlled_buffer_1_out_2[6], controlled_buffer_1_out} = decoder_1_mem_t ? reg_2_out_5 : 8'bz;  // Controlled_Buffer controlled_buffer_2
  ALU alu_1 (
    .in_4(reg_3_out_5), .in_5(reg_4_out_5), .in_6(reg_4_out_6), .in_7(clock_1_out),
    .in_8(decoder_1_alu_flag), .in_9(decoder_1_alu_rd), .in_1(decoder_1_bsel), .in_2(decoder_1_asel),
    .in_3(decoder_1_outsel), .out_10(decoder_1_dbus), .out_11(alu_1_out_11), .out_12(alu_1_out_12),
    .out_13(alu_1_out_13), .out_14(alu_1_out_14));
  or or_1 (or_1_out, decoder_1_mem_read, decoder_1_mem_write);
  and and_1 (and_1_out, ~controlled_buffer_1_out_2[6], ~controlled_buffer_1_out_3[7], or_1_out);  // AND_Gate
  and and_2 (and_2_out, controlled_buffer_1_out_3[7], or_1_out);
  and and_3 (and_3_out, ~controlled_buffer_1_out[3], ~controlled_buffer_1_out[4], ~controlled_buffer_1_out[5], controlled_buffer_1_out_2[6], ~controlled_buffer_1_out_3[7]);  // AND_Gate
  not not_1 (not_1_out, decoder_1_mem_write);
  vidmem vidmem_1 (
    .in_1(controlled_buffer_1_out[2:0]), .in_2(decoder_1_dbus), .in_3(and_3_out), .in_4(decoder_1_mem_write),
    .in_5(decoder_1_mem_read), .in_6(clock_1_out), .out_7(vidmem_1_out_7), .out_8(vidmem_1_out_8),
    .out_9(vidmem_1_out_9), .out_10(vidmem_1_out_10), .out_11(vidmem_1_out_11), .out_12(vidmem_1_out_12),
    .out_13(vidmem_1_out_13), .out_14(vidmem_1_out_14), .out_15(decoder_1_dbus));
  RAM #(.addrWidth(6)) ram_1 (
    .addr(controlled_buffer_1_out), .data(decoder_1_dbus), .sel(and_1_out), .clk(clock_1_out), .ld(not_1_out));  // open: clr
  ROM #(.addrWidth(7)) rom_1 (
    .addr({controlled_buffer_1_out_2[6], controlled_buffer_1_out}), .data(decoder_1_dbus), .sel(and_2_out));
  DotMatrix #(.inputtype("row"), .matrixcols(8), .matrixrows(8)) dotmatrix_1 (
    .row0(vidmem_1_out_7), .row1(vidmem_1_out_8), .row2(vidmem_1_out_9), .row3(vidmem_1_out_10),
    .row4(vidmem_1_out_11), .row5(vidmem_1_out_12), .row6(vidmem_1_out_13), .row7(vidmem_1_out_14));
  nor nor_1 (nor_1_out, reg_3_out_5[0], reg_3_out_5[1], reg_3_out_5[2], reg_3_out_5[3], reg_3_out_5[4], reg_3_out_5[5], reg_3_out_5[6], reg_3_out_5[7]);
  not not_2 (not_2_out, nor_1_out);
  nor nor_2 (nor_2_out, reg_4_out_5[0], reg_4_out_5[1], reg_4_out_5[2], reg_4_out_5[3], reg_4_out_5[4], reg_4_out_5[5], reg_4_out_5[6], reg_4_out_5[7]);
  not not_3 (not_3_out, nor_2_out);

  // Notes on the sheet:
  //   T
  //   A
  //   B
  //   contents of rom_1 (hex, n*v repeats v):
  //   3 43 30 71 0 32 3 33 51 f5 71 50 6a 91 12 80 32 f4 70 13 98 33 2a 88 12 25 40 24
endmodule

module ALU_CORE_BIT (
  input  in_1,
  input  in_2,
  input  in_3,
  input  in_4,
  output out_5,
  output out_6
);

  wire and_1_out, and_2_out, and_3_out, and_4_out, nand_1_out, nor_2_out, or_1_out, or_2_out;

  nand nand_1 (nand_1_out, in_1, in_2);
  or or_1 (or_1_out, in_3, in_4);
  and and_1 (and_1_out, nand_1_out, or_1_out);
  and and_2 (and_2_out, in_3, in_4);
  or or_2 (or_2_out, nand_1_out, in_3, in_4);
  nor nor_1 (out_6, and_1_out, and_2_out);
  and and_3 (and_3_out, nand_1_out, in_3, in_4);
  and and_4 (and_4_out, out_6, or_2_out);
  nor nor_2 (nor_2_out, and_3_out, and_4_out);
  not not_1 (out_5, nor_2_out);
endmodule

module ALU_CORE (
  input  in_1,
  input  in_2,
  input  [7:0] in_3,
  input  [7:0] in_4,
  output [7:0] out_5,
  output out_6
);

  wire alu_core_bit_1_out_6, alu_core_bit_2_out_6, alu_core_bit_3_out_6, alu_core_bit_4_out_6,
       alu_core_bit_5_out_6, alu_core_bit_6_out_6, alu_core_bit_7_out_6;

  ALU_CORE_BIT alu_core_bit_1 (
    .in_3(in_3[0]), .in_4(in_4[0]), .out_5(out_5[0]), .in_1(in_1), .in_2(in_2), .out_6(alu_core_bit_1_out_6));
  ALU_CORE_BIT alu_core_bit_2 (
    .in_3(in_3[1]), .in_4(in_4[1]), .out_5(out_5[1]), .in_1(in_1), .in_2(alu_core_bit_1_out_6),
    .out_6(alu_core_bit_2_out_6));
  ALU_CORE_BIT alu_core_bit_3 (
    .in_3(in_3[2]), .in_4(in_4[2]), .out_5(out_5[2]), .in_1(in_1), .in_2(alu_core_bit_2_out_6),
    .out_6(alu_core_bit_3_out_6));
  ALU_CORE_BIT alu_core_bit_4 (
    .in_3(in_3[3]), .in_4(in_4[3]), .out_5(out_5[3]), .in_1(in_1), .in_2(alu_core_bit_3_out_6),
    .out_6(alu_core_bit_4_out_6));
  ALU_CORE_BIT alu_core_bit_5 (
    .in_3(in_3[4]), .in_4(in_4[4]), .out_5(out_5[4]), .in_1(in_1), .in_2(alu_core_bit_4_out_6),
    .out_6(alu_core_bit_5_out_6));
  ALU_CORE_BIT alu_core_bit_6 (
    .in_3(in_3[5]), .in_4(in_4[5]), .out_5(out_5[5]), .in_1(in_1), .in_2(alu_core_bit_5_out_6),
    .out_6(alu_core_bit_6_out_6));
  ALU_CORE_BIT alu_core_bit_7 (
    .in_3(in_3[6]), .in_4(in_4[6]), .out_5(out_5[6]), .in_1(in_1), .in_2(alu_core_bit_6_out_6),
    .out_6(alu_core_bit_7_out_6));
  ALU_CORE_BIT alu_core_bit_8 (
    .in_3(in_3[7]), .in_4(in_4[7]), .out_5(out_5[7]), .in_1(in_1), .in_2(alu_core_bit_7_out_6), .out_6(out_6));
endmodule

module ALU_ASEL (
  input  in_1,
  input  [7:0] in_2,
  output [7:0] out_3
);

  nand nand_1 (out_3[0], in_1, in_2[0]);
  nand nand_2 (out_3[1], in_1, in_2[1]);
  nand nand_3 (out_3[2], in_1, in_2[2]);
  nand nand_4 (out_3[3], in_1, in_2[3]);
  nand nand_5 (out_3[4], in_1, in_2[4]);
  nand nand_6 (out_3[5], in_1, in_2[5]);
  nand nand_7 (out_3[6], in_1, in_2[6]);
  nand nand_8 (out_3[7], in_1, in_2[7]);
endmodule

module ALU_BSEL (
  input  [1:0] in_1,
  input  [1:0] in_2,
  input  [7:0] in_3,
  input  [7:0] in_4,
  output [7:0] out_5
);

  wire and_1_out, and_2_out, and_3_out, and_4_out, and_5_out, and_6_out, and_7_out, and_8_out, and_9_out,
       and_10_out, and_11_out, and_12_out, and_13_out, and_14_out, and_15_out, and_16_out, and_17_out,
       and_18_out, and_19_out, and_20_out, and_21_out, and_22_out, and_23_out, and_24_out, nor_1_out,
       or_1_out, or_2_out, or_3_out, or_4_out, or_5_out, or_6_out, or_7_out, or_8_out;

  nor nor_1 (nor_1_out, in_2[1], in_2[0]);
  and and_1 (and_1_out, in_2[1], in_3[0]);
  or or_1 (or_1_out, and_1_out, and_2_out);
  and and_2 (and_2_out, in_1[1], in_4[0]);
  and and_3 (and_3_out, in_2[1], in_3[1]);
  or or_2 (or_2_out, and_3_out, and_4_out);
  and and_4 (and_4_out, in_1[1], in_4[1]);
  and and_5 (and_5_out, in_2[1], in_3[2]);
  or or_3 (or_3_out, and_5_out, and_6_out);
  and and_6 (and_6_out, in_1[1], in_4[2]);
  and and_7 (and_7_out, in_2[1], in_3[3]);
  or or_4 (or_4_out, and_7_out, and_8_out);
  and and_8 (and_8_out, in_1[1], in_4[3]);
  and and_9 (and_9_out, in_2[1], in_3[4]);
  or or_5 (or_5_out, and_9_out, and_10_out);
  and and_10 (and_10_out, in_1[1], in_4[4]);
  and and_11 (and_11_out, in_2[1], in_3[5]);
  or or_6 (or_6_out, and_11_out, and_12_out);
  and and_12 (and_12_out, in_1[1], in_4[5]);
  and and_13 (and_13_out, in_2[1], in_3[6]);
  or or_7 (or_7_out, and_13_out, and_14_out);
  and and_14 (and_14_out, in_1[1], in_4[6]);
  and and_15 (and_15_out, in_2[1], in_3[7]);
  or or_8 (or_8_out, and_15_out, and_16_out);
  and and_16 (and_16_out, in_1[1], in_4[7]);
  and and_17 (and_17_out, in_2[0], or_1_out);
  and and_18 (and_18_out, in_2[0], or_2_out);
  and and_19 (and_19_out, in_2[0], or_3_out);
  and and_20 (and_20_out, in_2[0], or_4_out);
  and and_21 (and_21_out, in_2[0], or_5_out);
  and and_22 (and_22_out, in_2[0], or_6_out);
  and and_23 (and_23_out, in_2[0], or_7_out);
  and and_24 (and_24_out, in_2[0], or_8_out);
  nor nor_2 (out_5[0], and_17_out, nor_1_out);
  nor nor_3 (out_5[1], and_18_out, nor_1_out);
  nor nor_4 (out_5[2], and_19_out, nor_1_out);
  nor nor_5 (out_5[3], and_20_out, nor_1_out);
  nor nor_6 (out_5[4], and_21_out, nor_1_out);
  nor nor_7 (out_5[5], and_22_out, nor_1_out);
  nor nor_8 (out_5[6], and_23_out, nor_1_out);
  nor nor_9 (out_5[7], and_24_out, nor_1_out);
endmodule

module ALU (
  input  [1:0] in_1,
  input  in_2,
  input  [2:0] in_3,
  input  [7:0] in_4,
  input  [7:0] in_5,
  input  [7:0] in_6,
  input  in_7,
  input  in_8,
  input  in_9,
  output [7:0] out_10,
  output out_11,
  output out_12,
  output out_13,
  output out_14
);

  wire alu_core_1_out_6, alu_outsel_1_out_10, and_1_out, nand_1_out, nand_2_out, nand_3_out, nor_2_out,
       not_4_out, or_1_out, or_2_out;
  wire [1:0] not_2_out;
  wire [1:1] not_1_out;
  wire [2:0] not_3_out;
  wire [7:0] alu_asel_1_out_3, alu_bsel_1_out_5, alu_core_1_out_5, alu_outsel_1_out_9;

  and and_1 (and_1_out, not_3_out[2], in_3[1]);
  nor nor_1 (not_2_out[1], and_1_out, in_1[1]);
  not not_1 (not_1_out[1], not_2_out[1]);
  not not_2 (not_2_out[0], in_1[0]);
  ALU_ASEL alu_asel_1 (.in_2(in_4), .in_1(in_2), .out_3(alu_asel_1_out_3));
  ALU_BSEL alu_bsel_1 (
    .in_3(in_5), .in_4(in_6), .in_1(not_2_out), .in_2({not_1_out[1], in_1[0]}), .out_5(alu_bsel_1_out_5));
  // Probe on alu_asel_1_out_3
  assign not_3_out = ~in_3;  // NOT_Gate not_3, 3 bits wide
  or or_1 (or_1_out, in_3[0], not_3_out[1], not_3_out[2]);
  nand nand_1 (nand_1_out, not_3_out[1], not_3_out[0]);
  ALU_CORE alu_core_1 (
    .in_3(alu_asel_1_out_3), .in_4(alu_bsel_1_out_5), .out_5(alu_core_1_out_5), .in_1(nand_1_out),
    .in_2(nand_2_out), .out_6(alu_core_1_out_6));
  not not_4 (not_4_out, alu_core_1_out_6);
  // Probe on alu_bsel_1_out_5
  or or_2 (or_2_out, out_12, in_3[1]);
  nand nand_2 (nand_2_out, or_1_out, or_2_out);
  nor nor_2 (nor_2_out, alu_outsel_1_out_9[0], alu_outsel_1_out_9[1], alu_outsel_1_out_9[2], alu_outsel_1_out_9[3], alu_outsel_1_out_9[4], alu_outsel_1_out_9[5], alu_outsel_1_out_9[6], alu_outsel_1_out_9[7]);
  nand nand_3 (nand_3_out, in_1[1], out_11);
  ALU_OUTSEL alu_outsel_1 (
    .in_5(alu_core_1_out_5), .in_6(alu_asel_1_out_3), .in_7(alu_bsel_1_out_5), .out_9(alu_outsel_1_out_9),
    .MODE(not_3_out), .in_4(nand_3_out), .ALUC(not_4_out), .NMODE(in_3), .out_10(alu_outsel_1_out_10),
    .in_3(in_9));
  assign out_10 = in_9 ? alu_outsel_1_out_9 : 8'bz;  // Controlled_Buffer controlled_buffer_1
  D_Flip_Flop d_ff_1 (.clk(in_7), .D(alu_outsel_1_out_10), .Q(out_11), .Qn(out_12), .en(in_8));  // open: preset, reset
  D_Flip_Flop d_ff_2 (.clk(in_7), .D(nor_2_out), .Q(out_13), .Qn(out_14), .en(in_8));  // open: preset, reset
endmodule

module ALU_OUTSEL (
  input  [2:0] MODE,
  input  [2:0] NMODE,
  input  in_3,
  input  in_4,
  input  [7:0] in_5,
  input  [7:0] in_6,
  input  [7:0] in_7,
  input  ALUC,
  output [7:0] out_9,
  output out_10
);

  wire and_1_out, and_2_out, and_3_out, and_4_out, and_5_out, and_6_out, and_7_out, and_8_out, and_9_out,
       and_10_out, and_11_out, and_12_out, and_13_out, and_14_out, and_15_out, and_16_out, and_17_out,
       and_18_out, and_19_out, and_20_out, and_21_out, and_22_out, and_23_out, and_24_out, and_25_out,
       and_26_out, and_27_out, and_28_out, and_29_out, and_30_out, and_31_out, and_32_out, and_33_out,
       and_34_out, and_35_out, and_36_out, and_37_out, and_38_out, and_39_out, and_40_out, and_41_out,
       and_42_out, and_43_out, nor_1_out, nor_3_out, nor_4_out, nor_5_out, nor_14_out, not_1_out, or_1_out,
       or_2_out, or_3_out, or_4_out, or_5_out, or_6_out, or_7_out, or_8_out;

  nor nor_1 (nor_1_out, MODE[2], not_1_out);
  and and_1 (and_1_out, in_5[0], nor_3_out);
  and and_2 (and_2_out, in_5[7], nor_4_out);
  nor nor_2 (out_10, and_1_out, and_2_out, and_3_out);
  and and_3 (and_3_out, ALUC, nor_1_out);
  nor nor_3 (nor_3_out, NMODE[0], NMODE[2], MODE[1], not_1_out);
  nor nor_4 (nor_4_out, MODE[1], NMODE[2], MODE[0], not_1_out);
  and and_4 (and_4_out, nor_1_out, in_5[0]);
  and and_5 (and_5_out, nor_4_out, in_4);
  and and_6 (and_6_out, nor_3_out, in_5[1]);
  and and_7 (and_7_out, nor_5_out, in_6[0], in_7[0]);
  and and_8 (and_8_out, nor_14_out, or_1_out);
  or or_1 (or_1_out, in_6[0], in_7[0]);
  and and_9 (and_9_out, nor_1_out, in_5[1]);
  and and_10 (and_10_out, nor_4_out, in_5[0]);
  and and_11 (and_11_out, nor_3_out, in_5[2]);
  and and_12 (and_12_out, nor_5_out, in_6[1], in_7[1]);
  and and_13 (and_13_out, nor_14_out, or_2_out);
  or or_2 (or_2_out, in_6[1], in_7[1]);
  and and_14 (and_14_out, nor_1_out, in_5[2]);
  and and_15 (and_15_out, nor_4_out, in_5[1]);
  and and_16 (and_16_out, nor_3_out, in_5[3]);
  and and_17 (and_17_out, nor_5_out, in_6[2], in_7[2]);
  and and_18 (and_18_out, nor_14_out, or_3_out);
  or or_3 (or_3_out, in_6[2], in_7[2]);
  and and_19 (and_19_out, nor_1_out, in_5[3]);
  and and_20 (and_20_out, nor_4_out, in_5[2]);
  and and_21 (and_21_out, nor_3_out, in_5[4]);
  and and_22 (and_22_out, nor_5_out, in_6[3], in_7[3]);
  and and_23 (and_23_out, nor_14_out, or_4_out);
  or or_4 (or_4_out, in_6[3], in_7[3]);
  and and_24 (and_24_out, nor_1_out, in_5[4]);
  and and_25 (and_25_out, nor_4_out, in_5[3]);
  and and_26 (and_26_out, nor_3_out, in_5[5]);
  and and_27 (and_27_out, nor_5_out, in_6[4], in_7[4]);
  and and_28 (and_28_out, nor_14_out, or_5_out);
  or or_5 (or_5_out, in_6[4], in_7[4]);
  and and_29 (and_29_out, nor_1_out, in_5[5]);
  and and_30 (and_30_out, nor_4_out, in_5[4]);
  and and_31 (and_31_out, nor_3_out, in_5[6]);
  and and_32 (and_32_out, nor_5_out, in_6[5], in_7[5]);
  and and_33 (and_33_out, nor_14_out, or_6_out);
  or or_6 (or_6_out, in_6[5], in_7[5]);
  and and_34 (and_34_out, nor_1_out, in_5[6]);
  and and_35 (and_35_out, nor_4_out, in_5[5]);
  and and_36 (and_36_out, nor_3_out, in_5[7]);
  and and_37 (and_37_out, nor_5_out, in_6[6], in_7[6]);
  and and_38 (and_38_out, nor_14_out, or_7_out);
  or or_7 (or_7_out, in_6[6], in_7[6]);
  and and_39 (and_39_out, nor_1_out, in_5[7]);
  and and_40 (and_40_out, nor_4_out, in_5[6]);
  and and_41 (and_41_out, nor_3_out, in_4);
  and and_42 (and_42_out, nor_5_out, in_6[7], in_7[7]);
  and and_43 (and_43_out, nor_14_out, or_8_out);
  or or_8 (or_8_out, in_6[7], in_7[7]);
  nor nor_5 (nor_5_out, NMODE[1], NMODE[2], NMODE[0], not_1_out);
  nor nor_6 (out_9[0], and_4_out, and_5_out, and_6_out, and_7_out, and_8_out);
  nor nor_7 (out_9[1], and_9_out, and_10_out, and_11_out, and_12_out, and_13_out);
  nor nor_8 (out_9[2], and_14_out, and_15_out, and_16_out, and_17_out, and_18_out);
  nor nor_9 (out_9[3], and_19_out, and_20_out, and_21_out, and_22_out, and_23_out);
  nor nor_10 (out_9[4], and_24_out, and_25_out, and_26_out, and_27_out, and_28_out);
  nor nor_11 (out_9[5], and_29_out, and_30_out, and_31_out, and_32_out, and_33_out);
  nor nor_12 (out_9[6], and_34_out, and_35_out, and_36_out, and_37_out, and_38_out);
  nor nor_13 (out_9[7], and_39_out, and_40_out, and_41_out, and_42_out, and_43_out);
  not not_1 (not_1_out, in_3);
  nor nor_14 (nor_14_out, NMODE[1], NMODE[2], MODE[0], not_1_out);
endmodule

module REG (
  input  [7:0] in_1,
  input  in_2,
  input  in_3,
  input  in_4,
  output [7:0] out_5,
  output [7:0] out_6,
  output [7:0] out_7
);

  Pull_Resistor pull_resistor_1 (.node(in_4));
  D_Flip_Flop d_ff_1 (.clk(in_2), .D(in_1[0]), .Q(out_5[0]), .Qn(out_6[0]), .en(in_3));  // open: preset, reset
  D_Flip_Flop d_ff_2 (.clk(in_2), .D(in_1[1]), .Q(out_5[1]), .Qn(out_6[1]), .en(in_3));  // open: preset, reset
  D_Flip_Flop d_ff_3 (.clk(in_2), .D(in_1[2]), .Q(out_5[2]), .Qn(out_6[2]), .en(in_3));  // open: preset, reset
  D_Flip_Flop d_ff_4 (.clk(in_2), .D(in_1[3]), .Q(out_5[3]), .Qn(out_6[3]), .en(in_3));  // open: preset, reset
  D_Flip_Flop d_ff_5 (.clk(in_2), .D(in_1[4]), .Q(out_5[4]), .Qn(out_6[4]), .en(in_3));  // open: preset, reset
  D_Flip_Flop d_ff_6 (.clk(in_2), .D(in_1[5]), .Q(out_5[5]), .Qn(out_6[5]), .en(in_3));  // open: preset, reset
  D_Flip_Flop d_ff_7 (.clk(in_2), .D(in_1[6]), .Q(out_5[6]), .Qn(out_6[6]), .en(in_3));  // open: preset, reset
  D_Flip_Flop d_ff_8 (.clk(in_2), .D(in_1[7]), .Q(out_5[7]), .Qn(out_6[7]), .en(in_3));  // open: preset, reset
  assign out_7 = in_4 ? ~out_6 : 8'bz;  // Controlled_Inverter controlled_inverter_1
endmodule

module PC (
  input  [7:0] in_1,
  input  in_2,
  input  in_3,
  input  in_4,
  input  in_5,
  output [7:0] out_6
);

  wire and_1_out, and_2_out, and_3_out, and_4_out, and_5_out, and_6_out, and_7_out, and_8_out, and_9_out,
       and_10_out, and_11_out, and_12_out, and_13_out, and_14_out, and_15_out, and_16_out, and_17_out,
       and_18_out, and_19_out, and_20_out, and_21_out, and_22_out, and_23_out, and_24_out, and_25_out,
       and_26_out, and_27_out, and_28_out, and_29_out, and_30_out, and_31_out, and_32_out, nor_1_out,
       nor_2_out, nor_3_out, nor_4_out, nor_5_out, nor_6_out, not_1_out, not_2_out, not_3_out, not_4_out,
       not_5_out, not_6_out, not_7_out, not_8_out, not_9_out, not_10_out, not_11_out, not_12_out, not_13_out,
       or_1_out, or_2_out, or_3_out, or_4_out, or_5_out, or_6_out, or_7_out, or_8_out, or_9_out, or_10_out,
       or_11_out, or_12_out, or_13_out, or_14_out, or_15_out, or_16_out, s_r_ff_1_qn, s_r_ff_2_qn,
       s_r_ff_3_qn, s_r_ff_4_qn, s_r_ff_5_qn, s_r_ff_6_qn, s_r_ff_7_qn, s_r_ff_8_qn, s_r_ff_9_q, s_r_ff_9_qn,
       s_r_ff_10_q, s_r_ff_10_qn, s_r_ff_11_q, s_r_ff_11_qn, s_r_ff_12_q, s_r_ff_12_qn, s_r_ff_13_q,
       s_r_ff_13_qn, s_r_ff_14_q, s_r_ff_14_qn, s_r_ff_15_q, s_r_ff_15_qn, s_r_ff_16_q, s_r_ff_16_qn;

  not not_1 (not_1_out, in_1[0]);
  not not_2 (not_2_out, in_1[1]);
  not not_3 (not_3_out, in_1[2]);
  not not_4 (not_4_out, in_1[3]);
  not not_5 (not_5_out, in_1[4]);
  not not_6 (not_6_out, in_1[5]);
  not not_7 (not_7_out, in_1[6]);
  not not_8 (not_8_out, in_1[7]);
  and and_1 (and_1_out, s_r_ff_9_qn, in_4);
  or or_1 (or_1_out, and_1_out, and_2_out);
  and and_2 (and_2_out, in_1[0], in_5);
  and and_3 (and_3_out, s_r_ff_9_q, in_4);
  or or_2 (or_2_out, and_3_out, and_4_out);
  and and_4 (and_4_out, not_1_out, in_5);
  and and_5 (and_5_out, s_r_ff_10_qn, s_r_ff_9_q, in_4);
  or or_3 (or_3_out, and_5_out, and_6_out);
  and and_6 (and_6_out, in_1[1], in_5);
  and and_7 (and_7_out, s_r_ff_10_q, s_r_ff_9_q, in_4);
  or or_4 (or_4_out, and_7_out, and_8_out);
  and and_8 (and_8_out, not_2_out, in_5);
  and and_9 (and_9_out, s_r_ff_11_qn, nor_1_out, in_4);
  or or_5 (or_5_out, and_9_out, and_10_out);
  and and_10 (and_10_out, in_1[2], in_5);
  and and_11 (and_11_out, s_r_ff_11_q, nor_1_out, in_4);
  or or_6 (or_6_out, and_11_out, and_12_out);
  and and_12 (and_12_out, not_3_out, in_5);
  and and_13 (and_13_out, s_r_ff_12_qn, nor_2_out, in_4);
  or or_7 (or_7_out, and_13_out, and_14_out);
  and and_14 (and_14_out, in_1[3], in_5);
  and and_15 (and_15_out, s_r_ff_12_q, nor_2_out, in_4);
  or or_8 (or_8_out, and_15_out, and_16_out);
  and and_16 (and_16_out, not_4_out, in_5);
  and and_17 (and_17_out, s_r_ff_13_qn, nor_3_out, in_4);
  or or_9 (or_9_out, and_17_out, and_18_out);
  and and_18 (and_18_out, in_1[4], in_5);
  and and_19 (and_19_out, s_r_ff_13_q, nor_3_out, in_4);
  or or_10 (or_10_out, and_19_out, and_20_out);
  and and_20 (and_20_out, not_5_out, in_5);
  and and_21 (and_21_out, s_r_ff_14_qn, nor_4_out, in_4);
  or or_11 (or_11_out, and_21_out, and_22_out);
  and and_22 (and_22_out, in_1[5], in_5);
  and and_23 (and_23_out, s_r_ff_14_q, nor_4_out, in_4);
  or or_12 (or_12_out, and_23_out, and_24_out);
  and and_24 (and_24_out, not_6_out, in_5);
  and and_25 (and_25_out, s_r_ff_15_qn, nor_5_out, in_4);
  or or_13 (or_13_out, and_25_out, and_26_out);
  and and_26 (and_26_out, in_1[6], in_5);
  and and_27 (and_27_out, s_r_ff_15_q, nor_5_out, in_4);
  or or_14 (or_14_out, and_27_out, and_28_out);
  and and_28 (and_28_out, not_7_out, in_5);
  and and_29 (and_29_out, s_r_ff_16_qn, nor_6_out, in_4);
  or or_15 (or_15_out, and_29_out, and_30_out);
  and and_30 (and_30_out, in_1[7], in_5);
  and and_31 (and_31_out, s_r_ff_16_q, nor_6_out, in_4);
  or or_16 (or_16_out, and_31_out, and_32_out);
  and and_32 (and_32_out, not_8_out, in_5);
  S_R_Flip_Flop s_r_ff_1 (
    .S(or_1_out), .clk(in_3), .R(or_2_out), .Q(out_6[0]), .Qn(s_r_ff_1_qn), .reset(in_2));  // open: preset, en
  S_R_Flip_Flop s_r_ff_2 (
    .S(or_3_out), .clk(in_3), .R(or_4_out), .Q(out_6[1]), .Qn(s_r_ff_2_qn), .reset(in_2));  // open: preset, en
  S_R_Flip_Flop s_r_ff_3 (
    .S(or_5_out), .clk(in_3), .R(or_6_out), .Q(out_6[2]), .Qn(s_r_ff_3_qn), .reset(in_2));  // open: preset, en
  S_R_Flip_Flop s_r_ff_4 (
    .S(or_7_out), .clk(in_3), .R(or_8_out), .Q(out_6[3]), .Qn(s_r_ff_4_qn), .reset(in_2));  // open: preset, en
  S_R_Flip_Flop s_r_ff_5 (
    .S(or_9_out), .clk(in_3), .R(or_10_out), .Q(out_6[4]), .Qn(s_r_ff_5_qn), .reset(in_2));  // open: preset, en
  S_R_Flip_Flop s_r_ff_6 (
    .S(or_11_out), .clk(in_3), .R(or_12_out), .Q(out_6[5]), .Qn(s_r_ff_6_qn), .reset(in_2));  // open: preset, en
  S_R_Flip_Flop s_r_ff_7 (
    .S(or_13_out), .clk(in_3), .R(or_14_out), .Q(out_6[6]), .Qn(s_r_ff_7_qn), .reset(in_2));  // open: preset, en
  S_R_Flip_Flop s_r_ff_8 (
    .S(or_15_out), .clk(in_3), .R(or_16_out), .Q(out_6[7]), .Qn(s_r_ff_8_qn), .preset(in_2));  // open: reset, en
  S_R_Flip_Flop #(.trigger("falling")) s_r_ff_9 (
    .S(out_6[0]), .clk(in_3), .R(s_r_ff_1_qn), .Q(s_r_ff_9_q), .Qn(s_r_ff_9_qn), .reset(in_2));  // open: preset, en
  S_R_Flip_Flop #(.trigger("falling")) s_r_ff_10 (
    .S(out_6[1]), .clk(in_3), .R(s_r_ff_2_qn), .Q(s_r_ff_10_q), .Qn(s_r_ff_10_qn), .reset(in_2));  // open: preset, en
  nor nor_1 (nor_1_out, s_r_ff_10_qn, s_r_ff_9_qn);
  not not_9 (not_9_out, nor_1_out);
  S_R_Flip_Flop #(.trigger("falling")) s_r_ff_11 (
    .S(out_6[2]), .clk(in_3), .R(s_r_ff_3_qn), .Q(s_r_ff_11_q), .Qn(s_r_ff_11_qn), .reset(in_2));  // open: preset, en
  nor nor_2 (nor_2_out, s_r_ff_11_qn, not_9_out);
  not not_10 (not_10_out, nor_2_out);
  S_R_Flip_Flop #(.trigger("falling")) s_r_ff_12 (
    .S(out_6[3]), .clk(in_3), .R(s_r_ff_4_qn), .Q(s_r_ff_12_q), .Qn(s_r_ff_12_qn), .reset(in_2));  // open: preset, en
  nor nor_3 (nor_3_out, s_r_ff_12_qn, not_10_out);
  not not_11 (not_11_out, nor_3_out);
  S_R_Flip_Flop #(.trigger("falling")) s_r_ff_13 (
    .S(out_6[4]), .clk(in_3), .R(s_r_ff_5_qn), .Q(s_r_ff_13_q), .Qn(s_r_ff_13_qn), .reset(in_2));  // open: preset, en
  nor nor_4 (nor_4_out, s_r_ff_13_qn, not_11_out);
  not not_12 (not_12_out, nor_4_out);
  S_R_Flip_Flop #(.trigger("falling")) s_r_ff_14 (
    .S(out_6[5]), .clk(in_3), .R(s_r_ff_6_qn), .Q(s_r_ff_14_q), .Qn(s_r_ff_14_qn), .reset(in_2));  // open: preset, en
  nor nor_5 (nor_5_out, s_r_ff_14_qn, not_12_out);
  not not_13 (not_13_out, nor_5_out);
  S_R_Flip_Flop #(.trigger("falling")) s_r_ff_15 (
    .S(out_6[6]), .clk(in_3), .R(s_r_ff_7_qn), .Q(s_r_ff_15_q), .Qn(s_r_ff_15_qn), .reset(in_2));  // open: preset, en
  nor nor_6 (nor_6_out, s_r_ff_15_qn, not_13_out);
  S_R_Flip_Flop #(.trigger("falling")) s_r_ff_16 (
    .S(out_6[7]), .clk(in_3), .R(s_r_ff_8_qn), .Q(s_r_ff_16_q), .Qn(s_r_ff_16_qn), .preset(in_2));  // open: reset, en
endmodule

module decoder (
  input  [7:0] in_1,
  input  [7:0] in_2,
  input  in_3,
  input  in_4,
  input  in_5,
  input  in_6,
  input  in_7,
  input  in_8,
  input  in_9,
  input  in_10,
  input  in_11,
  input  in_12,
  input  in_13,
  output PC_INC,
  output PC_WRT,
  output MEM_PC,
  output MEM_T,
  output MEM_READ,
  output MEM_WRITE,
  output IR_WRT,
  output A_WR,
  output B_WR,
  output T_RD,
  output T_WR,
  output ALU_RD,
  output ALU_FLAG,
  output ASEL,
  output [1:0] BSEL,
  output [2:0] OUTSEL,
  output [7:0] DBUS
);

  wire and_1_out, and_2_out, and_3_out, and_4_out, and_5_out, and_6_out, and_7_out, and_8_out, and_9_out,
       and_10_out, and_11_out, and_12_out, and_13_out, and_14_out, and_15_out, and_16_out, and_17_out,
       and_18_out, and_19_out, and_20_out, and_21_out, and_22_out, and_23_out, and_24_out, and_25_out,
       and_26_out, and_27_out, and_28_out, and_29_out, and_30_out, and_31_out, j_k_ff_1_q, nand_1_out,
       nand_2_out, nand_3_out, nand_4_out, nand_5_out, nand_6_out, nor_1_out, nor_4_out, nor_5_out,
       not_1_out, not_2_out, not_3_out, not_4_out, or_1_out, or_2_out, or_3_out, or_4_out, or_5_out,
       or_6_out, or_7_out, or_8_out, or_9_out, or_10_out, or_11_out, or_12_out, or_13_out, or_14_out,
       or_15_out, or_16_out, or_17_out, or_18_out, or_19_out, s_r_ff_1_q, s_r_ff_1_qn, s_r_ff_2_q,
       s_r_ff_2_qn, s_r_ff_3_q, s_r_ff_3_qn, s_r_ff_4_q, s_r_ff_4_qn, xor_1_out;

  and and_1 (and_1_out, s_r_ff_3_q, s_r_ff_4_qn);
  and and_2 (and_2_out, s_r_ff_3_q, s_r_ff_4_q);
  S_R_Flip_Flop #(.trigger("falling")) s_r_ff_1 (
    .S(s_r_ff_3_qn), .clk(in_4), .R(s_r_ff_3_q), .Q(s_r_ff_1_q), .Qn(s_r_ff_1_qn), .reset(in_3),
    .en(j_k_ff_1_q));  // open: preset
  S_R_Flip_Flop #(.trigger("falling")) s_r_ff_2 (
    .S(and_1_out), .clk(in_4), .R(and_2_out), .Q(s_r_ff_2_q), .Qn(s_r_ff_2_qn), .reset(in_3), .en(j_k_ff_1_q));  // open: preset
  nor nor_1 (nor_1_out, not_2_out, s_r_ff_1_q, in_1[7], in_2[5], in_1[4], in_1[3], in_2[2], in_1[1], in_1[0]);
  S_R_Flip_Flop s_r_ff_3 (
    .S(s_r_ff_1_q), .clk(in_4), .R(s_r_ff_1_qn), .Q(s_r_ff_3_q), .Qn(s_r_ff_3_qn), .reset(in_3),
    .en(j_k_ff_1_q));  // open: preset
  S_R_Flip_Flop s_r_ff_4 (
    .S(s_r_ff_2_q), .clk(in_4), .R(s_r_ff_2_qn), .Q(s_r_ff_4_q), .Qn(s_r_ff_4_qn), .reset(in_3),
    .en(j_k_ff_1_q));  // open: preset
  J_K_Flip_Flop j_k_ff_1 (
    .J(and_3_out), .clk(in_4), .K(nor_1_out), .Q(j_k_ff_1_q), .preset(in_3));  // open: Qn, en, reset
  and and_3 (and_3_out, in_1[6], in_13);
  not not_1 (not_1_out, s_r_ff_1_q);
  not not_2 (not_2_out, s_r_ff_2_q);
  or or_1 (or_1_out, in_2[2], in_1[0]);
  or or_2 (or_2_out, in_1[1], in_1[0]);
  or or_3 (or_3_out, in_1[3], and_4_out);
  and and_4 (and_4_out, in_2[1], or_1_out);
  and and_5 (and_5_out, in_2[3], in_2[2], in_2[1], in_2[0]);
  and and_6 (and_6_out, in_2[5], in_1[4]);
  and and_7 (and_7_out, in_1[5], in_2[4], in_2[3], in_2[2], or_2_out);
  and and_8 (and_8_out, in_2[3], in_1[2], or_4_out);
  or or_4 (or_4_out, in_1[1], in_1[0]);
  and and_9 (and_9_out, in_2[0], in_5);
  and and_10 (and_10_out, in_1[0], in_9);
  nand nand_1 (nand_1_out, in_2[7], in_1[5], in_2[4], or_3_out);
  nand nand_2 (nand_2_out, in_2[7], in_2[4], or_5_out);
  or or_5 (or_5_out, in_2[5], and_5_out);
  nand nand_3 (nand_3_out, in_2[7], or_6_out);
  or or_6 (or_6_out, and_6_out, and_7_out);
  nand nand_4 (nand_4_out, in_2[7], in_1[5], or_7_out);
  or or_7 (or_7_out, in_1[4], and_8_out);
  nand nand_5 (nand_5_out, in_2[7], in_1[5], in_2[4], in_1[3]);
  nand nand_6 (nand_6_out, in_2[7], in_1[5], in_2[4], in_2[3], in_1[1]);
  not not_3 (not_3_out, nand_5_out);
  or or_8 (or_8_out, in_7, in_2[0]);
  and and_11 (and_11_out, or_8_out, in_2[1]);
  and and_12 (and_12_out, in_1[1], or_9_out);
  or or_9 (or_9_out, and_9_out, and_10_out);
  or or_10 (or_10_out, nand_5_out, in_2[2], in_2[1], in_2[0]);
  or or_11 (or_11_out, and_11_out, and_12_out);
  and and_13 (and_13_out, or_11_out, in_2[2]);
  and and_14 (and_14_out, in_1[2], in_1[1], in_1[0]);
  and and_15 (and_15_out, in_11, in_1[2]);
  and and_16 (and_16_out, not_3_out, not_4_out);
  or or_12 (or_12_out, s_r_ff_1_q, nand_1_out);
  or or_13 (or_13_out, not_1_out, nand_3_out);
  and and_17 (and_17_out, in_1[2], in_1[1], in_1[0]);
  and and_18 (and_18_out, nand_4_out, or_10_out);
  and and_19 (and_19_out, in_1[6], in_2[7]);
  nor nor_2 (ASEL, and_19_out, and_20_out);
  and and_20 (and_20_out, in_1[5], in_1[7]);
  and and_21 (and_21_out, in_2[6], in_2[7]);
  nor nor_3 (BSEL[0], and_21_out, and_22_out);
  and and_22 (and_22_out, in_1[3], in_1[7]);
  nand nand_7 (BSEL[1], in_1[4], in_1[7]);
  nand nand_8 (OUTSEL[0], in_1[0], in_1[7]);
  nand nand_9 (OUTSEL[1], in_1[1], in_1[7]);
  nand nand_10 (OUTSEL[2], in_1[2], in_1[7]);
  and and_23 (and_23_out, in_1[5], in_2[4]);
  nor nor_4 (nor_4_out, and_13_out, and_14_out, and_15_out);
  and and_24 (and_24_out, s_r_ff_2_q, or_14_out);
  or or_14 (or_14_out, nand_1_out, and_16_out);
  and and_25 (and_25_out, s_r_ff_2_q, nand_1_out);
  and and_26 (and_26_out, nand_3_out, nand_4_out);
  or or_15 (or_15_out, s_r_ff_2_q, s_r_ff_1_q);
  or or_16 (or_16_out, not_2_out, and_27_out);
  and and_27 (and_27_out, or_12_out, or_13_out);
  and and_28 (and_28_out, in_2[7], nand_2_out, nand_3_out);
  and and_29 (and_29_out, in_2[7], nand_2_out, nand_3_out);
  and and_30 (and_30_out, in_2[7], nand_2_out, or_17_out);
  or or_17 (or_17_out, nand_5_out, and_17_out, xor_1_out);
  or or_18 (or_18_out, in_2[7], s_r_ff_1_q);
  and and_31 (and_31_out, or_18_out, or_19_out);
  or or_19 (or_19_out, not_1_out, and_18_out);
  nor nor_5 (nor_5_out, s_r_ff_1_q, not_2_out, in_1[7], and_23_out);
  xor xor_1 (xor_1_out, in_1[6], nor_4_out);
  nor nor_6 (PC_INC, not_1_out, and_24_out);
  nor nor_7 (PC_WRT, not_1_out, not_2_out, nand_5_out, xor_1_out);
  nor nor_8 (MEM_PC, s_r_ff_1_q, and_25_out);
  nor nor_9 (MEM_T, not_1_out, not_2_out, and_26_out);
  nand nand_11 (MEM_READ, or_15_out, or_16_out);
  nor nor_10 (MEM_WRITE, not_2_out, not_1_out, nand_4_out);
  nor nor_11 (IR_WRT, s_r_ff_2_q, s_r_ff_1_q);
  nor nor_12 (A_WR, not_1_out, not_2_out, in_1[6], and_28_out);
  nor nor_13 (B_WR, not_1_out, not_2_out, in_2[6], and_29_out);
  nor nor_14 (T_RD, not_2_out, not_1_out, and_30_out);
  nor nor_15 (T_WR, not_2_out, s_r_ff_1_q);
  nor nor_16 (ALU_RD, not_2_out, and_31_out);
  nor nor_17 (ALU_FLAG, not_2_out, s_r_ff_1_q, in_2[7]);
  assign DBUS = nor_5_out ? {4'b0000, in_1[3:0]} : 8'bz;  // Controlled_Buffer controlled_buffer_1
  not not_4 (not_4_out, xor_1_out);

  // Notes on the sheet:
  //   ARG
  //   LIMM
  //   LMem
  //   SMem
  //   JMP
  //   IND
endmodule

module vidmem (
  input  [2:0] in_1,
  input  [7:0] in_2,
  input  in_3,
  input  in_4,
  input  in_5,
  input  in_6,
  output [7:0] out_7,
  output [7:0] out_8,
  output [7:0] out_9,
  output [7:0] out_10,
  output [7:0] out_11,
  output [7:0] out_12,
  output [7:0] out_13,
  output [7:0] out_14,
  output [7:0] out_15
);

  wire and_1_out, and_2_out, decoder_1_out0, decoder_1_out1, decoder_1_out2, decoder_1_out3, decoder_1_out4,
       decoder_1_out5, decoder_1_out6, decoder_1_out7;

  and and_1 (and_1_out, in_3, in_4);
  and and_2 (and_2_out, in_3, in_5);
  Decoder #(.select(3), .disabled(0)) decoder_1 (
    .out0(decoder_1_out0), .out1(decoder_1_out1), .out2(decoder_1_out2), .out3(decoder_1_out3),
    .out4(decoder_1_out4), .out5(decoder_1_out5), .out6(decoder_1_out6), .out7(decoder_1_out7), .sel(in_1),
    .en(and_1_out));
  Register register_1 (.D(in_2), .en(decoder_1_out0), .Q(out_7), .clk(in_6));  // open: clr
  Register register_2 (.D(in_2), .en(decoder_1_out1), .Q(out_8), .clk(in_6));  // open: clr
  Register register_3 (.D(in_2), .en(decoder_1_out2), .Q(out_9), .clk(in_6));  // open: clr
  Register register_4 (.en(decoder_1_out3), .Q(out_10), .clk(in_6));  // open: D, clr
  Register register_5 (.D(in_2), .en(decoder_1_out4), .Q(out_11), .clk(in_6));  // open: clr
  Register register_6 (.D(in_2), .en(decoder_1_out5), .Q(out_12), .clk(in_6));  // open: clr
  Register register_7 (.D(in_2), .en(decoder_1_out6), .Q(out_13), .clk(in_6));  // open: clr
  Register register_8 (.D(in_2), .en(decoder_1_out7), .Q(out_14), .clk(in_6));  // open: clr
  Demultiplexer #(.select(3), .width(8)) demultiplexer_1 (
    .out0(out_7), .out1(out_8), .out2(out_9), .out3(out_10), .out4(out_11), .out5(out_12), .out6(out_13),
    .out7(out_14), .in(out_15), .sel(in_1), .en(and_2_out));
endmodule
